# Fritzing sketch A330_FCU (saved by Fritzing 0.9.3b)
circuit board: 40cm x 10cm

parts:
  LED_SPD = LED - 3mm [color="Orange (612nm)" package="3 mm [THT]"]  # not connected
  LED_HDG = LED - 3mm [color="Orange (612nm)" package="3 mm [THT]"]  # not connected
  LED_LVL/CH = LED - 3mm [color="Orange (612nm)" package="3 mm [THT]"]  # not connected
  IC1 = IC, DIP package, 28 pins [chip_label=MCP23017]
  SEL_HDG = Rotary Encoder [package=THT]  # not connected
  SEL_ND_MODE = Rotary_Switch_12x1  # not connected
  SEL_SPD = Rotary Encoder [package=THT]  # not connected
  SEL_ALT = Rotary Encoder [package=THT]  # not connected
  SEL_V/S = Rotary Encoder [package=THT]  # not connected
  IC2 = IC, DIP package, 28 pins [chip_label=MCP23017]
  IC3 = IC, DIP package, 28 pins [chip_label=MCP23017]
  IC4 = IC, DIP package, 24 pins [chip_label=MAX7219]
  IC5 = IC, DIP package, 24 pins [chip_label=MAX7219]
  DSP_SPD3 = 7 Segment Display
  DSP_SPD2 = 7 Segment Display
  DSP_HDG1 = 7 Segment Display
  DSP_HDG2 = 7 Segment Display
  DSP_HDG3 = 7 Segment Display
  DSP_ALT1 = 7 Segment Display
  DSP_ALT2 = 7 Segment Display
  DSP_ALT3 = 7 Segment Display
  DSP_ALT4 = 7 Segment Display
  DSP_ALT5 = 7 Segment Display
  DSP_V/S1 = 7 Segment Display
  DSP_V/S2 = 7 Segment Display
  DSP_V/S3 = 7 Segment Display
  DSP_V/S4 = 7 Segment Display
  DSP_V/S5 = 7 Segment Display
  DSP_SPD1 = 7 Segment Display
  WeMos_D1_Mini = WeMos D1 Mini
  LED_MASTER_WARN = LED - 3mm [color="Red (635nm)" package="3 mm [THT]"]  # not connected
  R2 = Resistor [tolerance=±5% resistance=10k package=THT]
  R1 = Resistor [tolerance=±5% resistance=10k package=THT]
  C1 = Ceramic Capacitor [capacitance=0.1µF part_number=IC4 package="100 mil [THT, multilayer]"]
  C2 = Ceramic Capacitor [capacitance=0.1µF part_number=IC5 package="100 mil [THT, multilayer]"]
  Bauteil1 = Logic Level Converter
  BTN_MASTER_WARN = Pushbutton [package="[THT]"]  # not connected
  BTN_MASTER_CAUT = Pushbutton [package="[THT]"]  # not connected
  LED_MASTER_CAUT = LED - 3mm [color="Red (635nm)" package="3 mm [THT]"]  # not connected
  BTN_FD = Pushbutton [package="[THT]"]  # not connected
  LED_FD = LED - 3mm [color="Green (560nm)" package="3 mm [THT]"]  # not connected
  BTN_LS = Pushbutton [package="[THT]"]  # not connected
  LED_LS = LED - 3mm [color="Green (560nm)" package="3 mm [THT]"]  # not connected
  BTN_CSTR = Pushbutton [package="[THT]"]  # not connected
  BTN_WPT = Pushbutton [package="[THT]"]  # not connected
  LED_WPT = LED - 3mm [color="Green (560nm)" package="3 mm [THT]"]  # not connected
  LED_CSTR = LED - 3mm [color="Green (560nm)" package="3 mm [THT]"]  # not connected
  BTN_NDB = Pushbutton [package="[THT]"]  # not connected
  BTN_VOR_D = Pushbutton [package="[THT]"]  # not connected
  LED_NDB = LED - 3mm [color="Green (560nm)" package="3 mm [THT]"]  # not connected
  LED_VOR_D = LED - 3mm [color="Green (560nm)" package="3 mm [THT]"]  # not connected
  BTN_ARPT = Pushbutton [package="[THT]"]  # not connected
  LED_ARPT = LED - 3mm [color="Green (560nm)" package="3 mm [THT]"]  # not connected
  BTN_AP1 = Pushbutton [package="[THT]"]  # not connected
  BTN_AP2 = Pushbutton [package="[THT]"]  # not connected
  BTN_LOC = Pushbutton [package="[THT]"]  # not connected
  LED_LOC = LED - 3mm [color="Green (560nm)" package="3 mm [THT]"]  # not connected
  LED_AP1 = LED - 3mm [color="Green (560nm)" package="3 mm [THT]"]  # not connected
  LED_AP2 = LED - 3mm [color="Green (560nm)" package="3 mm [THT]"]  # not connected
  BTN_A/THR = Pushbutton [package="[THT]"]  # not connected
  LED_A/THR = LED - 3mm [color="Green (560nm)" package="3 mm [THT]"]  # not connected
  BTN_ALT = Pushbutton [package="[THT]"]  # not connected
  LED_ALT = LED - 3mm [color="Green (560nm)" package="3 mm [THT]"]  # not connected
  BTN_HDG_PULL = Pushbutton [package="[THT]"]  # not connected
  BTN_APPR = Pushbutton [package="[THT]"]  # not connected
  LED_APPR = LED - 3mm [color="Green (560nm)" package="3 mm [THT]"]  # not connected
  BTN_METRIC_ALT = Pushbutton [package="[THT]"]  # not connected
  BTN_SPD_MACH = Pushbutton [package="[THT]"]  # not connected
  BTN_HDG/TRK_VHS/FPA = Pushbutton [package="[THT]"]  # not connected
  BTN_SPD_PULL = Pushbutton [package="[THT]"]  # not connected
  BTN_ALT_PULL = Pushbutton [package="[THT]"]  # not connected
  BTN_V/S_PULL = Pushbutton [package="[THT]"]  # not connected
  SEL_ND_RNG = Rotary_Switch_12x1  # not connected

nets:
  SCL: IC1.pin12, IC2.pin12, IC3.pin12, WeMos_D1_Mini.D1
  SDA: IC1.pin13, IC2.pin13, IC3.pin13, WeMos_D1_Mini.D2
  MOSI: IC4.pin1, WeMos_D1_Mini.D7
  N1: IC4.pin2, DSP_SPD1.common_cathode
  N2: IC4.pin3, DSP_HDG2.common_cathode
  GND: IC4.pin4, IC4.pin9, IC5.pin4, IC5.pin9, WeMos_D1_Mini.G, C1.0, C2.0, Bauteil1.GND
  N3: IC4.pin5, DSP_ALT1.common_cathode
  N4: IC4.pin6, DSP_SPD3.common_cathode
  N5: IC4.pin7, DSP_HDG1.common_cathode
  N6: IC4.pin8, DSP_ALT2.common_cathode
  N7: IC4.pin10, DSP_HDG3.common_cathode
  N8: IC4.pin11, DSP_SPD2.common_cathode
  CS: IC4.pin12, IC5.pin12, WeMos_D1_Mini.D8
  CLK: IC4.pin13, IC5.pin13, WeMos_D1_Mini.D5
  N9: IC4.pin14, DSP_SPD3.Segment_A, DSP_SPD2.Segment_A, DSP_HDG1.Segment_A, DSP_HDG2.Segment_A, DSP_HDG3.Segment_A, DSP_ALT1.Segment_A, DSP_ALT2.Segment_A, DSP_SPD1.Segment_A
  N10: IC4.pin15, DSP_SPD3.Segment_F, DSP_SPD2.Segment_F, DSP_HDG1.Segment_F, DSP_HDG2.Segment_F, DSP_HDG3.Segment_F, DSP_ALT1.Segment_F, DSP_ALT2.Segment_F, DSP_SPD1.Segment_F
  N11: IC4.pin16, DSP_SPD3.Segment_B, DSP_SPD2.Segment_B, DSP_HDG1.Segment_B, DSP_HDG2.Segment_B, DSP_HDG3.Segment_B, DSP_ALT1.Segment_B, DSP_ALT2.Segment_B, DSP_SPD1.Segment_B
  N12: IC4.pin17, DSP_SPD3.Segment_G, DSP_SPD2.Segment_G, DSP_HDG1.Segment_G, DSP_HDG2.Segment_G, DSP_HDG3.Segment_G, DSP_ALT1.Segment_G, DSP_ALT2.Segment_G, DSP_SPD1.Segment_G
  N13: IC4.pin18, R1.Pin_0
  5V: IC4.pin19, IC5.pin19, WeMos_D1_Mini.5V, R2.Pin_1, R1.Pin_1, C1.1, C2.1, Bauteil1.HV
  N14: IC4.pin20, DSP_SPD3.Segment_C, DSP_SPD2.Segment_C, DSP_HDG1.Segment_C, DSP_HDG2.Segment_C, DSP_HDG3.Segment_C, DSP_ALT1.Segment_C, DSP_ALT2.Segment_C, DSP_SPD1.Segment_C
  N15: IC4.pin21, DSP_SPD3.Segment_E, DSP_SPD2.Segment_E, DSP_HDG1.Segment_E, DSP_HDG2.Segment_E, DSP_HDG3.Segment_E, DSP_ALT1.Segment_E, DSP_ALT2.Segment_E, DSP_SPD1.Segment_E
  N16: IC4.pin22, DSP_SPD3.Segment_DP, DSP_SPD2.Segment_DP, DSP_HDG1.Segment_DP, DSP_HDG2.Segment_DP, DSP_HDG3.Segment_DP, DSP_ALT1.Segment_DP, DSP_ALT2.Segment_DP, DSP_SPD1.Segment_DP
  N17: IC4.pin23, DSP_SPD3.Segment_D, DSP_SPD2.Segment_D, DSP_HDG1.Segment_D, DSP_HDG2.Segment_D, DSP_HDG3.Segment_D, DSP_ALT1.Segment_D, DSP_ALT2.Segment_D, DSP_SPD1.Segment_D
  N18: IC4.pin24, IC5.pin1
  N19: IC5.pin2, DSP_ALT3.common_cathode
  N20: IC5.pin3, DSP_V/S2.common_cathode
  N21: IC5.pin5, DSP_V/S4.common_cathode
  N22: IC5.pin6, DSP_ALT5.common_cathode
  N23: IC5.pin7, DSP_V/S1.common_cathode
  N24: IC5.pin8, DSP_V/S5.common_cathode
  N25: IC5.pin10, DSP_V/S3.common_cathode
  N26: IC5.pin11, DSP_ALT4.common_cathode
  N27: IC5.pin14, DSP_ALT3.Segment_A, DSP_ALT4.Segment_A, DSP_ALT5.Segment_A, DSP_V/S1.Segment_A, DSP_V/S2.Segment_A, DSP_V/S3.Segment_A, DSP_V/S4.Segment_A, DSP_V/S5.Segment_A
  N28: IC5.pin15, DSP_ALT3.Segment_F, DSP_ALT4.Segment_F, DSP_ALT5.Segment_F, DSP_V/S1.Segment_F, DSP_V/S2.Segment_F, DSP_V/S3.Segment_F, DSP_V/S4.Segment_F, DSP_V/S5.Segment_F
  N29: IC5.pin16, DSP_ALT3.Segment_B, DSP_ALT4.Segment_B, DSP_ALT5.Segment_B, DSP_V/S1.Segment_B, DSP_V/S2.Segment_B, DSP_V/S3.Segment_B, DSP_V/S4.Segment_B, DSP_V/S5.Segment_B
  N30: IC5.pin17, DSP_ALT3.Segment_G, DSP_ALT4.Segment_G, DSP_ALT5.Segment_G, DSP_V/S1.Segment_G, DSP_V/S2.Segment_G, DSP_V/S3.Segment_G, DSP_V/S4.Segment_G, DSP_V/S5.Segment_G
  N31: IC5.pin18, R2.Pin_0
  N32: IC5.pin20, DSP_ALT3.Segment_C, DSP_ALT4.Segment_C, DSP_ALT5.Segment_C, DSP_V/S1.Segment_C, DSP_V/S2.Segment_C, DSP_V/S3.Segment_C, DSP_V/S4.Segment_C, DSP_V/S5.Segment_C
  N33: IC5.pin21, DSP_ALT3.Segment_E, DSP_ALT4.Segment_E, DSP_ALT5.Segment_E, DSP_V/S1.Segment_E, DSP_V/S2.Segment_E, DSP_V/S3.Segment_E, DSP_V/S4.Segment_E, DSP_V/S5.Segment_E
  N34: IC5.pin22, DSP_ALT3.Segment_DP, DSP_ALT4.Segment_DP, DSP_ALT5.Segment_DP, DSP_V/S1.Segment_DP, DSP_V/S2.Segment_DP, DSP_V/S3.Segment_DP, DSP_V/S4.Segment_DP, DSP_V/S5.Segment_DP
  N35: IC5.pin23, DSP_ALT3.Segment_D, DSP_ALT4.Segment_D, DSP_ALT5.Segment_D, DSP_V/S1.Segment_D, DSP_V/S2.Segment_D, DSP_V/S3.Segment_D, DSP_V/S4.Segment_D, DSP_V/S5.Segment_D
  3.3V: WeMos_D1_Mini.3V3, Bauteil1.LV
  MISO: WeMos_D1_Mini.D6
