# Fritzing sketch A330_FCU_ArdSimX (saved by Fritzing 0.9.3b)

parts:
  LED_SPD = LED - 3mm [color="Orange (612nm)" package="3 mm [THT]"]  # not connected
  LED_HDG = LED - 3mm [color="Orange (612nm)" package="3 mm [THT]"]  # not connected
  LED_LVL/CH = LED - 3mm [color="Orange (612nm)" package="3 mm [THT]"]  # not connected
  SEL_HDG = Rotary Encoder [package=THT]  # not connected
  SEL_ND_MODE = Rotary_Switch_12x1  # not connected
  SEL_SPD = Rotary Encoder [package=THT]  # not connected
  SEL_ALT = Rotary Encoder [package=THT]  # not connected
  SEL_V/S = Rotary Encoder [package=THT]  # not connected
  DSP_SPD3 = 7 Segment Display
  DSP_SPD2 = 7 Segment Display
  DSP_HDG1 = 7 Segment Display
  DSP_HDG2 = 7 Segment Display
  DSP_HDG3 = 7 Segment Display
  DSP_ALT1 = 7 Segment Display
  DSP_ALT2 = 7 Segment Display
  DSP_ALT3 = 7 Segment Display
  DSP_ALT4 = 7 Segment Display
  DSP_ALT5 = 7 Segment Display
  DSP_V/S1 = 7 Segment Display  # not connected
  DSP_V/S2 = 7 Segment Display  # not connected
  DSP_V/S3 = 7 Segment Display  # not connected
  DSP_V/S4 = 7 Segment Display  # not connected
  DSP_V/S5 = 7 Segment Display  # not connected
  LED_MASTER_WARN = LED - 3mm [color="Red (635nm)" package="3 mm [THT]"]  # not connected
  C1 = Ceramic Capacitor [capacitance=0.1µF part_number=IC4 package="100 mil [THT, multilayer]"]
  C2 = Ceramic Capacitor [capacitance=0.1µF part_number=IC5 package="100 mil [THT, multilayer]"]
  BTN_MASTER_WARN = Pushbutton [package="[THT]"]  # not connected
  BTN_MASTER_CAUT = Pushbutton [package="[THT]"]  # not connected
  LED_MASTER_CAUT = LED - 3mm [color="Red (635nm)" package="3 mm [THT]"]  # not connected
  BTN_FD = Pushbutton [package="[THT]"]  # not connected
  LED_FD = LED - 3mm [color="Green (560nm)" package="3 mm [THT]"]  # not connected
  BTN_LS = Pushbutton [package="[THT]"]  # not connected
  LED_LS = LED - 3mm [color="Green (560nm)" package="3 mm [THT]"]  # not connected
  BTN_CSTR = Pushbutton [package="[THT]"]  # not connected
  BTN_WPT = Pushbutton [package="[THT]"]  # not connected
  LED_WPT = LED - 3mm [color="Green (560nm)" package="3 mm [THT]"]  # not connected
  LED_CSTR = LED - 3mm [color="Green (560nm)" package="3 mm [THT]"]  # not connected
  BTN_NDB = Pushbutton [package="[THT]"]  # not connected
  BTN_VOR_D = Pushbutton [package="[THT]"]  # not connected
  LED_NDB = LED - 3mm [color="Green (560nm)" package="3 mm [THT]"]  # not connected
  LED_VOR_D = LED - 3mm [color="Green (560nm)" package="3 mm [THT]"]  # not connected
  BTN_ARPT = Pushbutton [package="[THT]"]  # not connected
  LED_ARPT = LED - 3mm [color="Green (560nm)" package="3 mm [THT]"]  # not connected
  BTN_AP1 = Pushbutton [package="[THT]"]  # not connected
  BTN_AP2 = Pushbutton [package="[THT]"]  # not connected
  BTN_LOC = Pushbutton [package="[THT]"]  # not connected
  LED_LOC = LED - 3mm [color="Green (560nm)" package="3 mm [THT]"]  # not connected
  LED_AP1 = LED - 3mm [color="Green (560nm)" package="3 mm [THT]"]  # not connected
  LED_AP2 = LED - 3mm [color="Green (560nm)" package="3 mm [THT]"]  # not connected
  BTN_A/THR = Pushbutton [package="[THT]"]  # not connected
  LED_A/THR = LED - 3mm [color="Green (560nm)" package="3 mm [THT]"]  # not connected
  BTN_ALT = Pushbutton [package="[THT]"]  # not connected
  LED_ALT = LED - 3mm [color="Green (560nm)" package="3 mm [THT]"]  # not connected
  BTN_HDG_PULL = Pushbutton [package="[THT]"]  # not connected
  BTN_APPR = Pushbutton [package="[THT]"]  # not connected
  LED_APPR = LED - 3mm [color="Green (560nm)" package="3 mm [THT]"]  # not connected
  BTN_METRIC_ALT = Pushbutton [package="[THT]"]  # not connected
  BTN_SPD_MACH = Pushbutton [package="[THT]"]  # not connected
  BTN_HDG/TRK_VHS/FPA = Pushbutton [package="[THT]"]  # not connected
  BTN_SPD_PULL = Pushbutton [package="[THT]"]  # not connected
  BTN_ALT_PULL = Pushbutton [package="[THT]"]  # not connected
  BTN_V/S_PULL = Pushbutton [package="[THT]"]  # not connected
  SEL_ND_RNG = Rotary_Switch_12x1  # not connected
  SR_LED1 = 74HC595 [package="DIP16 [THT]"]  # not connected
  SR_LED2 = 74HC595 [package="DIP16 [THT]"]  # not connected
  SR_SPD1 = 74HC595 [package="DIP16 [THT]"]
  SR_SPD2 = 74HC595 [package="DIP16 [THT]"]
  SR_SPD3 = 74HC595 [package="DIP16 [THT]"]
  SR_HDG1 = 74HC595 [package="DIP16 [THT]"]
  SR_HDG2 = 74HC595 [package="DIP16 [THT]"]
  SR_HDG3 = 74HC595 [package="DIP16 [THT]"]
  SR_ALT3 = 74HC595 [package="DIP16 [THT]"]  # not connected
  SR_ALT2 = 74HC595 [package="DIP16 [THT]"]  # not connected
  SR_ALT1 = 74HC595 [package="DIP16 [THT]"]  # not connected
  SR_ALT4 = 74HC595 [package="DIP16 [THT]"]  # not connected
  SR_ALT5 = 74HC595 [package="DIP16 [THT]"]  # not connected
  SR_V/S3 = 74HC595 [package="DIP16 [THT]"]  # not connected
  SR_V/S2 = 74HC595 [package="DIP16 [THT]"]  # not connected
  SR_V/S1 = 74HC595 [package="DIP16 [THT]"]  # not connected
  SR_V/S4 = 74HC595 [package="DIP16 [THT]"]  # not connected
  SR_V/S5 = 74HC595 [package="DIP16 [THT]"]  # not connected
  Bauteil1 = Arduino Mega 2560 (Rev3)  # not connected
  D1 = Diode [package=diode-1n4148]  # not connected
  R1 = Resistor [tolerance=±5% resistance=220 package=THT]
  R2 = Resistor [tolerance=±5% resistance=220 package=THT]
  R3 = Resistor [tolerance=±5% resistance=220 package=THT]
  R4 = Resistor [tolerance=±5% resistance=220 package=THT]
  R5 = Resistor [tolerance=±5% resistance=220 package=THT]
  R6 = Resistor [tolerance=±5% resistance=220 package=THT]
  R7 = Resistor [tolerance=±5% resistance=220 package=THT]
  R8 = Resistor [tolerance=±5% resistance=220 package=THT]
  DSP_SPD1 = 7 Segment Display
  R9 = Resistor [tolerance=±5% resistance=220 package=THT]
  R10 = Resistor [tolerance=±5% resistance=220 package=THT]
  R11 = Resistor [tolerance=±5% resistance=220 package=THT]
  R12 = Resistor [tolerance=±5% resistance=220 package=THT]
  R13 = Resistor [tolerance=±5% resistance=220 package=THT]
  R14 = Resistor [tolerance=±5% resistance=220 package=THT]
  R15 = Resistor [tolerance=±5% resistance=220 package=THT]
  R16 = Resistor [tolerance=±5% resistance=220 package=THT]
  R17 = Resistor [tolerance=±5% resistance=220 package=THT]
  R18 = Resistor [tolerance=±5% resistance=220 package=THT]
  R19 = Resistor [tolerance=±5% resistance=220 package=THT]
  R20 = Resistor [tolerance=±5% resistance=220 package=THT]
  R21 = Resistor [tolerance=±5% resistance=220 package=THT]
  R22 = Resistor [tolerance=±5% resistance=220 package=THT]
  R23 = Resistor [tolerance=±5% resistance=220 package=THT]
  R24 = Resistor [tolerance=±5% resistance=220 package=THT]
  R25 = Resistor [tolerance=±5% resistance=220 package=THT]
  R26 = Resistor [tolerance=±5% resistance=220 package=THT]
  R27 = Resistor [tolerance=±5% resistance=220 package=THT]
  R28 = Resistor [tolerance=±5% resistance=220 package=THT]
  R29 = Resistor [tolerance=±5% resistance=220 package=THT]
  R30 = Resistor [tolerance=±5% resistance=220 package=THT]
  R31 = Resistor [tolerance=±5% resistance=220 package=THT]
  R32 = Resistor [tolerance=±5% resistance=220 package=THT]
  R33 = Resistor [tolerance=±5% resistance=220 package=THT]
  R34 = Resistor [tolerance=±5% resistance=220 package=THT]
  R35 = Resistor [tolerance=±5% resistance=220 package=THT]
  R36 = Resistor [tolerance=±5% resistance=220 package=THT]
  R37 = Resistor [tolerance=±5% resistance=220 package=THT]
  R38 = Resistor [tolerance=±5% resistance=220 package=THT]
  R39 = Resistor [tolerance=±5% resistance=220 package=THT]
  R40 = Resistor [tolerance=±5% resistance=220 package=THT]
  R41 = Resistor [tolerance=±5% resistance=220 package=THT]
  R42 = Resistor [tolerance=±5% resistance=220 package=THT]
  R43 = Resistor [tolerance=±5% resistance=220 package=THT]
  R44 = Resistor [tolerance=±5% resistance=220 package=THT]
  R45 = Resistor [tolerance=±5% resistance=220 package=THT]
  R46 = Resistor [tolerance=±5% resistance=220 package=THT]
  R47 = Resistor [tolerance=±5% resistance=220 package=THT]
  R48 = Resistor [tolerance=±5% resistance=220 package=THT]
  R49 = Resistor [tolerance=±5% resistance=220 package=THT]
  R50 = Resistor [tolerance=±5% resistance=220 package=THT]
  R51 = Resistor [tolerance=±5% resistance=220 package=THT]
  R52 = Resistor [tolerance=±5% resistance=220 package=THT]
  R53 = Resistor [tolerance=±5% resistance=220 package=THT]
  R54 = Resistor [tolerance=±5% resistance=220 package=THT]
  R55 = Resistor [tolerance=±5% resistance=220 package=THT]
  R56 = Resistor [tolerance=±5% resistance=220 package=THT]
  R57 = Resistor [tolerance=±5% resistance=220 package=THT]
  R58 = Resistor [tolerance=±5% resistance=220 package=THT]
  R59 = Resistor [tolerance=±5% resistance=220 package=THT]
  R60 = Resistor [tolerance=±5% resistance=220 package=THT]
  R61 = Resistor [tolerance=±5% resistance=220 package=THT]
  R62 = Resistor [tolerance=±5% resistance=220 package=THT]
  R63 = Resistor [tolerance=±5% resistance=220 package=THT]
  R64 = Resistor [tolerance=±5% resistance=220 package=THT]
  R65 = Resistor [tolerance=±5% resistance=220 package=THT]
  R66 = Resistor [tolerance=±5% resistance=220 package=THT]
  R67 = Resistor [tolerance=±5% resistance=220 package=THT]
  R68 = Resistor [tolerance=±5% resistance=220 package=THT]
  R69 = Resistor [tolerance=±5% resistance=220 package=THT]
  R70 = Resistor [tolerance=±5% resistance=220 package=THT]
  R71 = Resistor [tolerance=±5% resistance=220 package=THT]
  R72 = Resistor [tolerance=±5% resistance=220 package=THT]
  R73 = Resistor [tolerance=±5% resistance=220 package=THT]
  R74 = Resistor [tolerance=±5% resistance=220 package=THT]
  R75 = Resistor [tolerance=±5% resistance=220 package=THT]
  R76 = Resistor [tolerance=±5% resistance=220 package=THT]
  R77 = Resistor [tolerance=±5% resistance=220 package=THT]
  R78 = Resistor [tolerance=±5% resistance=220 package=THT]
  R79 = Resistor [tolerance=±5% resistance=220 package=THT]
  R80 = Resistor [tolerance=±5% resistance=220 package=THT]
  R81 = Resistor [tolerance=±5% resistance=220 package=THT]
  R82 = Resistor [tolerance=±5% resistance=220 package=THT]
  R83 = Resistor [tolerance=±5% resistance=220 package=THT]
  R84 = Resistor [tolerance=±5% resistance=220 package=THT]
  R85 = Resistor [tolerance=±5% resistance=220 package=THT]
  R86 = Resistor [tolerance=±5% resistance=220 package=THT]
  R87 = Resistor [tolerance=±5% resistance=220 package=THT]
  R88 = Resistor [tolerance=±5% resistance=220 package=THT]

nets:
  N1: DSP_SPD3.Segment_E, R19.Pin_1
  N2: DSP_SPD3.Segment_D, R22.Pin_1
  GND: DSP_SPD3.common_cathode, DSP_SPD2.common_cathode, DSP_HDG1.common_cathode, DSP_HDG2.common_cathode, DSP_HDG3.common_cathode, DSP_ALT1.common_cathode, DSP_ALT2.common_cathode, DSP_ALT3.common_cathode, DSP_ALT4.common_cathode, DSP_ALT5.common_cathode, C1.0, C2.0, SR_SPD1.GND, SR_SPD1.OE, SR_SPD2.GND, SR_SPD2.OE, SR_SPD3.GND, SR_SPD3.OE, SR_HDG1.GND, SR_HDG1.OE, SR_HDG2.GND, SR_HDG2.OE, SR_HDG3.GND, SR_HDG3.OE, DSP_SPD1.common_cathode
  N3: DSP_SPD3.Segment_C, R24.Pin_1
  N4: DSP_SPD3.Segment_DP, R21.Pin_1
  N5: DSP_SPD3.Segment_B, R18.Pin_1
  N6: DSP_SPD3.Segment_A, R17.Pin_1
  N7: DSP_SPD3.Segment_F, R20.Pin_1
  N8: DSP_SPD3.Segment_G, R23.Pin_1
  N9: DSP_SPD2.Segment_E, R13.Pin_1
  N10: DSP_SPD2.Segment_D, R12.Pin_1
  N11: DSP_SPD2.Segment_C, R11.Pin_1
  N12: DSP_SPD2.Segment_DP, R16.Pin_1
  N13: DSP_SPD2.Segment_B, R10.Pin_1
  N14: DSP_SPD2.Segment_A, R9.Pin_1
  N15: DSP_SPD2.Segment_F, R14.Pin_1
  N16: DSP_SPD2.Segment_G, R15.Pin_1
  N17: DSP_HDG1.Segment_E, R28.Pin_1
  N18: DSP_HDG1.Segment_D, R29.Pin_1
  N19: DSP_HDG1.Segment_C, R30.Pin_1
  N20: DSP_HDG1.Segment_DP, R25.Pin_1
  N21: DSP_HDG1.Segment_B, R31.Pin_1
  N22: DSP_HDG1.Segment_A, R32.Pin_1
  N23: DSP_HDG1.Segment_F, R27.Pin_1
  N24: DSP_HDG1.Segment_G, R26.Pin_1
  N25: DSP_HDG2.Segment_E, R36.Pin_1
  N26: DSP_HDG2.Segment_D, R37.Pin_1
  N27: DSP_HDG2.Segment_C, R38.Pin_1
  N28: DSP_HDG2.Segment_DP, R33.Pin_1
  N29: DSP_HDG2.Segment_B, R39.Pin_1
  N30: DSP_HDG2.Segment_A, R40.Pin_1
  N31: DSP_HDG2.Segment_F, R35.Pin_1
  N32: DSP_HDG2.Segment_G, R34.Pin_1
  N33: DSP_HDG3.Segment_E, R44.Pin_1
  N34: DSP_HDG3.Segment_D, R45.Pin_1
  N35: DSP_HDG3.Segment_C, R46.Pin_1
  N36: DSP_HDG3.Segment_DP, R41.Pin_1
  N37: DSP_HDG3.Segment_B, R47.Pin_1
  N38: DSP_HDG3.Segment_A, R48.Pin_1
  N39: DSP_HDG3.Segment_F, R43.Pin_1
  N40: DSP_HDG3.Segment_G, R42.Pin_1
  N41: DSP_ALT1.Segment_E, R52.Pin_1
  N42: DSP_ALT1.Segment_D, R53.Pin_1
  N43: DSP_ALT1.Segment_C, R54.Pin_1
  N44: DSP_ALT1.Segment_DP, R49.Pin_1
  N45: DSP_ALT1.Segment_B, R55.Pin_1
  N46: DSP_ALT1.Segment_A, R56.Pin_1
  N47: DSP_ALT1.Segment_F, R51.Pin_1
  N48: DSP_ALT1.Segment_G, R50.Pin_1
  N49: DSP_ALT2.Segment_E, R60.Pin_1
  N50: DSP_ALT2.Segment_D, R61.Pin_1
  N51: DSP_ALT2.Segment_C, R62.Pin_1
  N52: DSP_ALT2.Segment_DP, R57.Pin_1
  N53: DSP_ALT2.Segment_B, R63.Pin_1
  N54: DSP_ALT2.Segment_A, R64.Pin_1
  N55: DSP_ALT2.Segment_F, R59.Pin_1
  N56: DSP_ALT2.Segment_G, R58.Pin_1
  N57: DSP_ALT3.Segment_E, R68.Pin_1
  N58: DSP_ALT3.Segment_D, R69.Pin_1
  N59: DSP_ALT3.Segment_C, R70.Pin_1
  N60: DSP_ALT3.Segment_DP, R65.Pin_1
  N61: DSP_ALT3.Segment_B, R71.Pin_1
  N62: DSP_ALT3.Segment_A, R72.Pin_1
  N63: DSP_ALT3.Segment_F, R67.Pin_1
  N64: DSP_ALT3.Segment_G, R66.Pin_1
  N65: DSP_ALT4.Segment_E, R76.Pin_1
  N66: DSP_ALT4.Segment_D, R77.Pin_1
  N67: DSP_ALT4.Segment_C, R78.Pin_1
  N68: DSP_ALT4.Segment_DP, R73.Pin_1
  N69: DSP_ALT4.Segment_B, R79.Pin_1
  N70: DSP_ALT4.Segment_A, R80.Pin_1
  N71: DSP_ALT4.Segment_F, R75.Pin_1
  N72: DSP_ALT4.Segment_G, R74.Pin_1
  N73: DSP_ALT5.Segment_E, R84.Pin_1
  N74: DSP_ALT5.Segment_D, R85.Pin_1
  N75: DSP_ALT5.Segment_C, R86.Pin_1
  N76: DSP_ALT5.Segment_DP, R81.Pin_1
  N77: DSP_ALT5.Segment_B, R87.Pin_1
  N78: DSP_ALT5.Segment_A, R88.Pin_1
  N79: DSP_ALT5.Segment_F, R83.Pin_1
  N80: DSP_ALT5.Segment_G, R82.Pin_1
  5V: C1.1, C2.1, SR_SPD1.MR, SR_SPD1.VCC, SR_SPD2.MR, SR_SPD2.VCC, SR_SPD3.MR, SR_SPD3.VCC, SR_HDG1.MR, SR_HDG1.VCC, SR_HDG2.MR, SR_HDG2.VCC, SR_HDG3.MR, SR_HDG3.VCC
  DSP_SPD1_B: SR_SPD1.Q1, R2.Pin_0
  DSP_SPD1_C: SR_SPD1.Q2, R3.Pin_0
  DSP_SPD1_D: SR_SPD1.Q3, R4.Pin_0
  DSP_SPD1_E: SR_SPD1.Q4, R5.Pin_0
  DSP_SPD1_F: SR_SPD1.Q5, R6.Pin_0
  DSP_SPD1_G: SR_SPD1.Q6, R7.Pin_0
  DSP_SPD1_H: SR_SPD1.Q7, R8.Pin_0
  N81: SR_SPD1.Q7', SR_SPD2.DS
  S: SR_SPD1.SH_CP, SR_SPD2.SH_CP, SR_SPD3.SH_CP, SR_HDG1.SH_CP, SR_HDG2.SH_CP, SR_HDG3.SH_CP
  L: SR_SPD1.ST_CP, SR_SPD2.ST_CP, SR_SPD3.ST_CP, SR_HDG1.ST_CP, SR_HDG2.ST_CP, SR_HDG3.ST_CP
  D_SPD: SR_SPD1.DS
  DSP_SPD1_A: SR_SPD1.Q0, R1.Pin_0
  DSP_SPD2_B: SR_SPD2.Q1, R10.Pin_0
  DSP_SPD2_C: SR_SPD2.Q2, R11.Pin_0
  DSP_SPD2_D: SR_SPD2.Q3, R12.Pin_0
  DSP_SPD2_E: SR_SPD2.Q4, R13.Pin_0
  DSP_SPD2_F: SR_SPD2.Q5, R14.Pin_0
  DSP_SPD2_G: SR_SPD2.Q6, R15.Pin_0
  DSP_SPD2_H: SR_SPD2.Q7, R16.Pin_0
  N82: SR_SPD2.Q7', SR_SPD3.DS
  DSP_SPD2_A: SR_SPD2.Q0, R9.Pin_0
  DSP_SPD3_B: SR_SPD3.Q1, R18.Pin_0
  DSP_SPD3_C: SR_SPD3.Q2, R24.Pin_0
  DSP_SPD3_D: SR_SPD3.Q3, R22.Pin_0
  DSP_SPD3_E: SR_SPD3.Q4, R19.Pin_0
  DSP_SPD3_F: SR_SPD3.Q5, R20.Pin_0
  DSP_SPD3_G: SR_SPD3.Q6, R23.Pin_0
  DSP_SPD3_H: SR_SPD3.Q7, R21.Pin_0
  DSP_SPD3_A: SR_SPD3.Q0, R17.Pin_0
  DSP_HDG1_B: SR_HDG1.Q1, R31.Pin_0
  DSP_HDG1_C: SR_HDG1.Q2, R30.Pin_0
  DSP_HDG1_D: SR_HDG1.Q3, R29.Pin_0
  DSP_HDG1_E: SR_HDG1.Q4, R28.Pin_0
  DSP_HDG1_F: SR_HDG1.Q5, R27.Pin_0
  DSP_HDG1_G: SR_HDG1.Q6, R26.Pin_0
  DSP_HDG1_H: SR_HDG1.Q7, R25.Pin_0
  N83: SR_HDG1.Q7', SR_HDG2.DS
  D_HDG: SR_HDG1.DS
  DSP_HDG1_A: SR_HDG1.Q0, R32.Pin_0
  DSP_HDG2_B: SR_HDG2.Q1, R39.Pin_0
  DSP_HDG2_C: SR_HDG2.Q2, R38.Pin_0
  DSP_HDG2_D: SR_HDG2.Q3, R37.Pin_0
  DSP_HDG2_E: SR_HDG2.Q4, R36.Pin_0
  DSP_HDG2_F: SR_HDG2.Q5, R35.Pin_0
  DSP_HDG2_G: SR_HDG2.Q6, R34.Pin_0
  DSP_HDG2_H: SR_HDG2.Q7, R33.Pin_0
  N84: SR_HDG2.Q7', SR_HDG3.DS
  DSP_HDG2_A: SR_HDG2.Q0, R40.Pin_0
  DSP_HDG3_B: SR_HDG3.Q1, R47.Pin_0
  DSP_HDG3_C: SR_HDG3.Q2, R46.Pin_0
  DSP_HDG3_D: SR_HDG3.Q3, R45.Pin_0
  DSP_HDG3_E: SR_HDG3.Q4, R44.Pin_0
  DSP_HDG3_F: SR_HDG3.Q5, R43.Pin_0
  DSP_HDG3_G: SR_HDG3.Q6, R42.Pin_0
  DSP_HDG3_H: SR_HDG3.Q7, R41.Pin_0
  DSP_HDG3_A: SR_HDG3.Q0, R48.Pin_0
  N85: R1.Pin_1, DSP_SPD1.Segment_A
  N86: R2.Pin_1, DSP_SPD1.Segment_B
  N87: R3.Pin_1, DSP_SPD1.Segment_C
  N88: R4.Pin_1, DSP_SPD1.Segment_D
  N89: R5.Pin_1, DSP_SPD1.Segment_E
  N90: R6.Pin_1, DSP_SPD1.Segment_F
  N91: R7.Pin_1, DSP_SPD1.Segment_G
  N92: R8.Pin_1, DSP_SPD1.Segment_DP
  DSP_ALT1_H: R49.Pin_0
  DSP_ALT1_G: R50.Pin_0
  DSP_ALT1_F: R51.Pin_0
  DSP_ALT1_E: R52.Pin_0
  DSP_ALT1_D: R53.Pin_0
  DSP_ALT1_C: R54.Pin_0
  DSP_ALT1_B: R55.Pin_0
  DSP_ALT1_A: R56.Pin_0
  DSP_ALT2_H: R57.Pin_0
  DSP_ALT2_G: R58.Pin_0
  DSP_ALT2_F: R59.Pin_0
  DSP_ALT2_E: R60.Pin_0
  DSP_ALT2_D: R61.Pin_0
  DSP_ALT2_C: R62.Pin_0
  DSP_ALT2_B: R63.Pin_0
  DSP_ALT2_A: R64.Pin_0
  DSP_ALT3_H: R65.Pin_0
  DSP_ALT3_G: R66.Pin_0
  DSP_ALT3_F: R67.Pin_0
  DSP_ALT3_E: R68.Pin_0
  DSP_ALT3_D: R69.Pin_0
  DSP_ALT3_C: R70.Pin_0
  DSP_ALT3_B: R71.Pin_0
  DSP_ALT3_A: R72.Pin_0
  DSP_ALT4_H: R73.Pin_0
  DSP_ALT4_G: R74.Pin_0
  DSP_ALT4_F: R75.Pin_0
  DSP_ALT4_E: R76.Pin_0
  DSP_ALT4_D: R77.Pin_0
  DSP_ALT4_C: R78.Pin_0
  DSP_ALT4_B: R79.Pin_0
  DSP_ALT4_A: R80.Pin_0
  DSP_ALT5_H: R81.Pin_0
  DSP_ALT5_G: R82.Pin_0
  DSP_ALT5_F: R83.Pin_0
  DSP_ALT5_E: R84.Pin_0
  DSP_ALT5_D: R85.Pin_0
  DSP_ALT5_C: R86.Pin_0
  DSP_ALT5_B: R87.Pin_0
  DSP_ALT5_A: R88.Pin_0
